# Fritzing sketch Multi-Sensor (saved by Fritzing 0.9.3b)

parts:
  U1 = ATTINY45 [package=dip]
  U2 = FS1000A - 433Mhz RF Transmitter [package=THT]
  PIR1 = PIR sensor
  M1 = BMP280
  Onderdeel1 = LilyPad Coin Cell Battery Holder

nets:
  N1: U1.PB4(ADC2), U2.DATA
  GND: U1.GND, U2.GND, PIR1.GND, M1.GND, Onderdeel1.-
  N2: U1.PB0(MOSI), M1.SDA
  N3: U1.PB1(MISO), PIR1.SIG
  N4: U1.PB2(SCK_ADC1), M1.SCL
  VCC: U1.VCC, U2.VCC, PIR1.VDD, M1.VIN, Onderdeel1.+

custom parts:
  FS1000A - 433Mhz RF Transmitter: This is 433Mhz RF transmitter with receiver kit for Arduino ARM MCU wireless Application environment: Remote control switch, receiver module, motorcycles, automobile anti-theft products, home security products, electric doors, shutter doors, windows, remote control socket, remote control LED, remote audio remote control electric doors, garage door remote control, remote control retractable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
  BMP280: Temperature Humidity Barometric presure Sensor, I2C
